// Logisim project hack-computer.circ as structural Verilog
module main (
  input  [15:0] Instruction,
  input  [15:0] InMemoryValue,
  input  ClkM,
  input  Reset,
  output WriteMemory,
  output [15:0] NextInstruction
);

  wire ALU_eq, ALU_gt, ALU_lt, and_1_out, and_2_out, ClkSync_out, multiplexer_4_out, not_1_out, not_2_out,
       not_3_out, or_1_out, or_2_out;
  wire [15:0] A_REG_q, ALU_out16, D_REG_q, multiplexer_1_out, multiplexer_2_out, multiplexer_3_out,
       ram_1_dout, rom_1_data;

  ROM #(.addrWidth(16), .dataWidth(16)) rom_1 (.addr(NextInstruction), .data(rom_1_data));
  // Probe on rom_1_data
  // Probe on rom_1_data[0]
  Multiplexer #(.width(16)) multiplexer_1 (
    .in0({16{1'b0}}), .in1(rom_1_data), .out({multiplexer_1_out[15:4], WriteMemory, multiplexer_1_out[2:0]}),
    .sel(rom_1_data[15]));
  // Probe on ram_1_dout
  // Probe on rom_1_data
  // Probe on multiplexer_1_out[6]
  // Probe on multiplexer_1_out[7]
  // Probe on multiplexer_1_out[8]
  // Probe on multiplexer_1_out[9]
  // Probe on multiplexer_1_out[10]
  // Probe on multiplexer_1_out[11]
  // Probe on multiplexer_1_out[12]
  not not_1 (not_1_out, rom_1_data[15]);
  Clock ClkSync (.out(ClkSync_out));
  or or_1 (or_1_out, ClkSync_out, ClkM);
  // Probe on multiplexer_1_out[5]
  // Probe on multiplexer_1_out[4]
  // Probe on WriteMemory
  // Probe on multiplexer_2_out
  Multiplexer #(.width(16)) multiplexer_2 (.in0(ALU_out16), .in1(rom_1_data), .out(multiplexer_2_out), .sel(not_1_out));
  or or_2 (or_2_out, multiplexer_1_out[5], not_1_out);
  // Probe on ALU_out16
  Register #(.trigger("falling"), .width(16)) A_REG (
    .D(multiplexer_2_out), .en(or_2_out), .clk(or_1_out), .Q(A_REG_q), .clr(Reset));
  Register #(.trigger("falling"), .width(16)) D_REG (
    .D(ALU_out16), .en(multiplexer_1_out[4]), .clk(or_1_out), .Q(D_REG_q), .clr(Reset));
  // Probe on multiplexer_1_out[0]
  // Probe on multiplexer_1_out[1]
  // Probe on multiplexer_1_out[2]
  // Probe on A_REG_q
  // Probe on A_REG_q
  // Probe on D_REG_q
  Multiplexer #(.width(16)) multiplexer_3 (
    .in0(A_REG_q), .in1(ram_1_dout), .out(multiplexer_3_out), .sel(multiplexer_1_out[12]));
  not not_2 (not_2_out, ALU_eq);
  // Probe on WriteMemory
  ALU16Bit ALU (
    .A(D_REG_q), .B(multiplexer_3_out), .ZX(multiplexer_1_out[11]), .NX(multiplexer_1_out[10]),
    .ZY(multiplexer_1_out[9]), .NY(multiplexer_1_out[8]), .F(multiplexer_1_out[7]),
    .NO(multiplexer_1_out[6]), .Out16(ALU_out16), .LT(ALU_lt), .EQ(ALU_eq), .GT(ALU_gt));
  and and_1 (and_1_out, ALU_eq, ALU_gt);
  and and_2 (and_2_out, ALU_eq, ALU_lt);
  // Probe on 1'b0
  // Probe on ALU_gt
  // Probe on ALU_eq
  // Probe on and_1_out
  // Probe on ALU_lt
  // Probe on not_2_out
  // Probe on and_2_out
  // Probe on 1'b1
  not not_3 (not_3_out, multiplexer_4_out);
  Multiplexer #(.select(3)) multiplexer_4 (
    .in0(1'b0), .in1(ALU_gt), .in2(ALU_eq), .in3(and_1_out), .in4(ALU_lt), .in5(not_2_out), .in6(and_2_out),
    .in7(1'b1), .out(multiplexer_4_out), .sel(multiplexer_1_out[2:0]));
  // Probe on A_REG_q
  // Probe on ALU_out16
  ProgramCounter PC (
    .Input16(A_REG_q), .Load(multiplexer_4_out), .Inc(not_3_out), .Clock(or_1_out), .Reset(Reset),
    .Output16(NextInstruction));
  RAM #(.addrWidth(16), .clearpin("true"), .dataWidth(16), .enables("line")) ram_1 (
    .addr(A_REG_q), .we(WriteMemory), .oe(1'b1), .clk(or_1_out), .din(ALU_out16), .dout(ram_1_dout),
    .clr(Reset));

  // Notes on the sheet:
  //   contents of rom_1 (hex, n*v repeats v):
  //   0 8c10 10 8308 a 8c10 11 8308 14 8c10 12 8308 11 9c10 3e 8302 12 9c10 3e 8302 11 9c10 12 94d0 0 8308
  //   0 9c10 2a 8301 11 9c10 1 8308 12 9c10 11 8308 1 9c10 12 8308 10 9c10 12 9090 10 8308 1 8c10 11 91d0
  //   11 8308 11 9c10 3e 8302 0 8c10 2a 8307 10 9c10
endmodule

module FullAdder1Bit (
  input  A,
  input  B,
  input  C,
  output SUM,
  output CAR
);

  wire and_1_out, and_2_out, xor_1_out;

  xor xor_1 (xor_1_out, A, B);
  and and_1 (and_1_out, A, B);
  xor xor_2 (SUM, xor_1_out, C);
  and and_2 (and_2_out, xor_1_out, C);
  or or_1 (CAR, and_1_out, and_2_out);
endmodule

module FullAdder16Bit (
  input  CARRY1,
  input  [15:0] A16,
  input  [15:0] B16,
  output [15:0] Out16
);

  wire BIT0_car, BIT1_car, BIT2_car, BIT3_car, BIT4_car, BIT5_car, BIT6_car, BIT7_car, BIT8_car, BIT9_car,
       BIT10_car, BIT11_car, BIT12_car, BIT13_car, BIT14_car, BIT15_car;

  FullAdder1Bit BIT0 (.A(A16[0]), .B(B16[0]), .C(CARRY1), .SUM(Out16[0]), .CAR(BIT0_car));
  FullAdder1Bit BIT1 (.A(A16[1]), .B(B16[1]), .C(BIT0_car), .SUM(Out16[1]), .CAR(BIT1_car));
  FullAdder1Bit BIT2 (.A(A16[2]), .B(B16[2]), .C(BIT1_car), .SUM(Out16[2]), .CAR(BIT2_car));
  FullAdder1Bit BIT3 (.A(A16[3]), .B(B16[3]), .C(BIT2_car), .SUM(Out16[3]), .CAR(BIT3_car));
  FullAdder1Bit BIT4 (.A(A16[4]), .B(B16[4]), .C(BIT3_car), .SUM(Out16[4]), .CAR(BIT4_car));
  FullAdder1Bit BIT5 (.A(A16[5]), .B(B16[5]), .C(BIT4_car), .SUM(Out16[5]), .CAR(BIT5_car));
  FullAdder1Bit BIT6 (.A(A16[6]), .B(B16[6]), .C(BIT5_car), .SUM(Out16[6]), .CAR(BIT6_car));
  FullAdder1Bit BIT7 (.A(A16[7]), .B(B16[7]), .C(BIT6_car), .SUM(Out16[7]), .CAR(BIT7_car));
  FullAdder1Bit BIT8 (.A(A16[8]), .B(B16[8]), .C(BIT7_car), .SUM(Out16[8]), .CAR(BIT8_car));
  FullAdder1Bit BIT9 (.A(A16[9]), .B(B16[9]), .C(BIT8_car), .SUM(Out16[9]), .CAR(BIT9_car));
  FullAdder1Bit BIT10 (.A(A16[10]), .B(B16[10]), .C(BIT9_car), .SUM(Out16[10]), .CAR(BIT10_car));
  FullAdder1Bit BIT11 (.A(A16[11]), .B(B16[11]), .C(BIT10_car), .SUM(Out16[11]), .CAR(BIT11_car));
  FullAdder1Bit BIT12 (.A(A16[12]), .B(B16[12]), .C(BIT11_car), .SUM(Out16[12]), .CAR(BIT12_car));
  FullAdder1Bit BIT13 (.A(A16[13]), .B(B16[13]), .C(BIT12_car), .SUM(Out16[13]), .CAR(BIT13_car));
  FullAdder1Bit BIT14 (.A(A16[14]), .B(B16[14]), .C(BIT13_car), .SUM(Out16[14]), .CAR(BIT14_car));
  FullAdder1Bit BIT15 (.A(A16[15]), .B(B16[15]), .C(BIT14_car), .SUM(Out16[15]), .CAR(BIT15_car));
  LED led_1 (.in(Out16[0]));
  LED led_2 (.in(Out16[1]));
  LED led_3 (.in(Out16[2]));
  LED led_4 (.in(Out16[3]));
  LED led_5 (.in(Out16[4]));
  LED led_6 (.in(Out16[5]));
  LED led_7 (.in(Out16[6]));
  LED led_8 (.in(Out16[7]));
  LED led_9 (.in(Out16[8]));
  LED led_10 (.in(Out16[9]));
  LED led_11 (.in(Out16[10]));
  LED led_12 (.in(Out16[11]));
  LED led_13 (.in(Out16[12]));
  LED led_14 (.in(Out16[13]));
  LED led_15 (.in(Out16[14]));
  LED led_16 (.in(Out16[15]));
  LED led_17 (.in(BIT15_car));
endmodule

module ALU16Bit (
  input  [15:0] A,
  input  [15:0] B,
  input  ZX,
  input  NX,
  input  ZY,
  input  NY,
  input  F,
  input  NO,
  output [15:0] Out16,
  output LT,
  output EQ,
  output GT
);

  wire adder_1_cout, not_4_out, or16to1bit_1_outp;
  wire [15:0] adder_1_out, and_1_out, multiplexer_1_out, multiplexer_2_out, multiplexer_3_out,
       multiplexer_4_out, multiplexer_5_out, not_1_out, not_2_out, not_3_out;

  Multiplexer #(.width(16)) multiplexer_1 (.in0(A), .in1({16{1'b0}}), .out(multiplexer_1_out), .sel(ZX));
  // Probe on multiplexer_1_out
  Multiplexer #(.width(16)) multiplexer_2 (.in0(B), .in1({16{1'b0}}), .out(multiplexer_2_out), .sel(ZY));
  // Probe on multiplexer_2_out
  assign not_1_out = ~multiplexer_1_out;  // NOT_Gate not_1, 16 bits wide
  assign not_2_out = ~multiplexer_2_out;  // NOT_Gate not_2, 16 bits wide
  // Probe on multiplexer_3_out
  Multiplexer #(.width(16)) multiplexer_3 (.in0(multiplexer_1_out), .in1(not_1_out), .out(multiplexer_3_out), .sel(NX));
  Multiplexer #(.width(16)) multiplexer_4 (.in0(multiplexer_2_out), .in1(not_2_out), .out(multiplexer_4_out), .sel(NY));
  // Probe on multiplexer_4_out
  assign and_1_out = multiplexer_3_out & multiplexer_4_out;  // AND_Gate and_1, 16 bits wide
  Adder #(.width(16)) adder_1 (
    .a(multiplexer_3_out), .b(multiplexer_4_out), .out(adder_1_out), .cout(adder_1_cout));  // open: cin
  // Probe on adder_1_out
  // Probe on and_1_out
  Multiplexer #(.width(16)) multiplexer_5 (.in0(and_1_out), .in1(adder_1_out), .out(multiplexer_5_out), .sel(F));
  // Probe on multiplexer_5_out
  // Probe on multiplexer_5_out
  assign not_3_out = ~multiplexer_5_out;  // NOT_Gate not_3, 16 bits wide
  // Probe on not_3_out
  Multiplexer #(.width(16)) multiplexer_6 (.in0(multiplexer_5_out), .in1(not_3_out), .out({LT, Out16[14:0]}), .sel(NO));
  // Probe on {LT, Out16[14:0]}
  // Probe on adder_1_cout
  not not_4 (not_4_out, LT);
  and and_2 (GT, not_4_out, or16to1bit_1_outp);
  Or16To1Bit or16to1bit_1 (.INP({LT, Out16[14:0]}), .Outp(or16to1bit_1_outp));
  not not_5 (EQ, or16to1bit_1_outp);

  assign Out16[15] = LT;
endmodule

module Incrementer16Bit (
  input  [15:0] Input16,
  output [15:0] Out16
);

  FullAdder16Bit fulladder16bit_1 (.CARRY1(1'b0), .A16(Input16), .B16(16'h1), .Out16(Out16));
endmodule

module Or16To1Bit (
  input  [15:0] INP,
  output Outp
);

  wire or_1_out, or_2_out, or_3_out, or_4_out, or_5_out, or_6_out, or_7_out, or_8_out, or_9_out, or_10_out,
       or_11_out, or_12_out, or_13_out, or_14_out;

  or or_1 (or_1_out, INP[0], INP[1]);
  or or_2 (or_2_out, INP[2], INP[3]);
  or or_3 (or_3_out, INP[4], INP[5]);
  or or_4 (or_4_out, INP[6], INP[7]);
  or or_5 (or_5_out, INP[8], INP[9]);
  or or_6 (or_6_out, INP[10], INP[11]);
  or or_7 (or_7_out, INP[12], INP[13]);
  or or_8 (or_8_out, INP[14], INP[15]);
  or or_9 (or_9_out, or_1_out, or_2_out);
  or or_10 (or_10_out, or_3_out, or_4_out);
  or or_11 (or_11_out, or_5_out, or_6_out);
  or or_12 (or_12_out, or_7_out, or_8_out);
  or or_13 (or_13_out, or_9_out, or_10_out);
  or or_14 (or_14_out, or_11_out, or_12_out);
  or or_15 (Outp, or_13_out, or_14_out);
endmodule

module DFlipFlop (
  input  D,
  input  CLOCK
);

  wire nand_1_out, nand_2_out, nand_3_out, nand_4_out, nand_5_out, nand_6_out, nand_7_out, nand_8_out,
       not_1_out, not_2_out, not_3_out;

  not not_1 (not_1_out, D);
  nand nand_1 (nand_1_out, D, CLOCK);
  nand nand_2 (nand_2_out, CLOCK, not_1_out);
  nand nand_3 (nand_3_out, nand_1_out, nand_4_out);
  nand nand_4 (nand_4_out, nand_3_out, nand_2_out);
  D_Flip_Flop #(.trigger("falling")) d_ff_1 (.D(D), .clk(CLOCK));  // open: Q, Qn, preset, reset
  not not_2 (not_2_out, nand_3_out);
  not not_3 (not_3_out, CLOCK);
  nand nand_5 (nand_5_out, nand_3_out, not_3_out);
  nand nand_6 (nand_6_out, not_3_out, not_2_out);
  nand nand_7 (nand_7_out, nand_5_out, nand_8_out);
  nand nand_8 (nand_8_out, nand_7_out, nand_6_out);
endmodule

module Register16Bit (
  input  [15:0] DATA,
  input  LOAD,
  input  CLOCK,
  output [15:0] Out16
);

  wire multiplexer_1_out, multiplexer_2_out, multiplexer_3_out, multiplexer_4_out, multiplexer_5_out,
       multiplexer_6_out, multiplexer_7_out, multiplexer_8_out, multiplexer_9_out, multiplexer_10_out,
       multiplexer_11_out, multiplexer_12_out, multiplexer_13_out, multiplexer_14_out, multiplexer_15_out,
       multiplexer_16_out;
  wire [15:0] register_1_q;

  Multiplexer multiplexer_1 (.in0(Out16[0]), .in1(DATA[0]), .out(multiplexer_1_out), .sel(LOAD));
  Multiplexer multiplexer_2 (.in0(Out16[1]), .in1(DATA[1]), .out(multiplexer_2_out), .sel(LOAD));
  Multiplexer multiplexer_3 (.in0(Out16[2]), .in1(DATA[2]), .out(multiplexer_3_out), .sel(CLOCK));
  Multiplexer multiplexer_4 (.in0(Out16[3]), .in1(DATA[3]), .out(multiplexer_4_out), .sel(CLOCK));
  D_Flip_Flop #(.trigger("falling")) d_ff_1 (
    .D(multiplexer_1_out), .clk(CLOCK), .Q(Out16[0]));  // open: Qn, preset, reset
  D_Flip_Flop #(.trigger("falling")) d_ff_2 (
    .D(multiplexer_2_out), .clk(CLOCK), .Q(Out16[1]));  // open: Qn, preset, reset
  D_Flip_Flop #(.trigger("falling")) d_ff_3 (
    .D(multiplexer_3_out), .clk(CLOCK), .Q(Out16[2]));  // open: Qn, preset, reset
  D_Flip_Flop #(.trigger("falling")) d_ff_4 (
    .D(multiplexer_4_out), .clk(CLOCK), .Q(Out16[3]));  // open: Qn, preset, reset
  Register #(.trigger("falling"), .width(16)) register_1 (
    .D(DATA), .en(LOAD), .clk(CLOCK), .Q(register_1_q));  // open: clr
  D_Flip_Flop #(.trigger("falling")) d_ff_5 (
    .D(multiplexer_5_out), .clk(CLOCK), .Q(Out16[4]));  // open: Qn, preset, reset
  Multiplexer multiplexer_5 (.in0(Out16[4]), .in1(DATA[4]), .out(multiplexer_5_out), .sel(LOAD));
  D_Flip_Flop #(.trigger("falling")) d_ff_6 (
    .D(multiplexer_6_out), .clk(CLOCK), .Q(Out16[5]));  // open: Qn, preset, reset
  Multiplexer multiplexer_6 (.in0(Out16[5]), .in1(DATA[5]), .out(multiplexer_6_out), .sel(LOAD));
  D_Flip_Flop #(.trigger("falling")) d_ff_7 (
    .D(multiplexer_7_out), .clk(CLOCK), .Q(Out16[6]));  // open: Qn, preset, reset
  Multiplexer multiplexer_7 (.in0(Out16[6]), .in1(DATA[6]), .out(multiplexer_7_out), .sel(LOAD));
  D_Flip_Flop #(.trigger("falling")) d_ff_8 (
    .D(multiplexer_8_out), .clk(CLOCK), .Q(Out16[7]));  // open: Qn, preset, reset
  Multiplexer multiplexer_8 (.in0(Out16[7]), .in1(DATA[7]), .out(multiplexer_8_out), .sel(LOAD));
  D_Flip_Flop #(.trigger("falling")) d_ff_9 (
    .D(multiplexer_9_out), .clk(CLOCK), .Q(Out16[8]));  // open: Qn, preset, reset
  Multiplexer multiplexer_9 (.in0(Out16[8]), .in1(DATA[8]), .out(multiplexer_9_out), .sel(LOAD));
  D_Flip_Flop #(.trigger("falling")) d_ff_10 (
    .D(multiplexer_10_out), .clk(CLOCK), .Q(Out16[9]));  // open: Qn, preset, reset
  Multiplexer multiplexer_10 (.in0(Out16[9]), .in1(DATA[9]), .out(multiplexer_10_out), .sel(LOAD));
  D_Flip_Flop #(.trigger("falling")) d_ff_11 (
    .D(multiplexer_11_out), .clk(CLOCK), .Q(Out16[10]));  // open: Qn, preset, reset
  Multiplexer multiplexer_11 (.in0(Out16[10]), .in1(DATA[10]), .out(multiplexer_11_out), .sel(LOAD));
  D_Flip_Flop #(.trigger("falling")) d_ff_12 (
    .D(multiplexer_12_out), .clk(LOAD), .Q(Out16[11]));  // open: Qn, preset, reset
  Multiplexer multiplexer_12 (.in0(Out16[11]), .in1(DATA[11]), .out(multiplexer_12_out), .sel(LOAD));
  D_Flip_Flop #(.trigger("falling")) d_ff_13 (
    .D(multiplexer_13_out), .clk(CLOCK), .Q(Out16[12]));  // open: Qn, preset, reset
  Multiplexer multiplexer_13 (.in0(Out16[12]), .in1(DATA[12]), .out(multiplexer_13_out), .sel(LOAD));
  D_Flip_Flop #(.trigger("falling")) d_ff_14 (
    .D(multiplexer_14_out), .clk(CLOCK), .Q(Out16[13]));  // open: Qn, preset, reset
  Multiplexer multiplexer_14 (.in0(Out16[13]), .in1(DATA[13]), .out(multiplexer_14_out), .sel(LOAD));
  D_Flip_Flop #(.trigger("falling")) d_ff_15 (
    .D(multiplexer_15_out), .clk(CLOCK), .Q(Out16[14]));  // open: Qn, preset, reset
  Multiplexer multiplexer_15 (.in0(Out16[14]), .in1(DATA[14]), .out(multiplexer_15_out), .sel(LOAD));
  D_Flip_Flop #(.trigger("falling")) d_ff_16 (
    .D(multiplexer_16_out), .clk(CLOCK), .Q(Out16[15]));  // open: Qn, preset, reset
  Multiplexer multiplexer_16 (.in0(Out16[15]), .in1(DATA[15]), .out(multiplexer_16_out), .sel(LOAD));
  // Probe on Out16
  // Probe on register_1_q
endmodule

module RAM8_64k (
  input  [15:0] In16,
  input  [2:0] Addr3,
  input  Load,
  input  Clock
);

  wire demultiplexer_2_out0, demultiplexer_2_out1, demultiplexer_2_out2, demultiplexer_2_out3,
       demultiplexer_2_out4, demultiplexer_2_out5, demultiplexer_2_out6, demultiplexer_2_out7,
       demultiplexer_3_out0, demultiplexer_3_out1, demultiplexer_3_out2, demultiplexer_3_out3,
       demultiplexer_3_out4, demultiplexer_3_out5, demultiplexer_3_out6, demultiplexer_3_out7;
  wire [15:0] demultiplexer_1_out0, demultiplexer_1_out1, demultiplexer_1_out2, demultiplexer_1_out3,
       demultiplexer_1_out4, demultiplexer_1_out5, demultiplexer_1_out6, demultiplexer_1_out7,
       multiplexer_1_out, register_1_q, register_2_q, register_3_q, register_4_q, register_5_q, register_6_q,
       register_7_q, register_8_q;

  Demultiplexer #(.select(3), .width(16)) demultiplexer_1 (
    .out0(demultiplexer_1_out0), .out1(demultiplexer_1_out1), .out2(demultiplexer_1_out2),
    .out3(demultiplexer_1_out3), .out4(demultiplexer_1_out4), .out5(demultiplexer_1_out5),
    .out6(demultiplexer_1_out6), .out7(demultiplexer_1_out7), .in(In16), .sel(Addr3));
  Demultiplexer #(.select(3)) demultiplexer_2 (
    .out0(demultiplexer_2_out0), .out1(demultiplexer_2_out1), .out2(demultiplexer_2_out2),
    .out3(demultiplexer_2_out3), .out4(demultiplexer_2_out4), .out5(demultiplexer_2_out5),
    .out6(demultiplexer_2_out6), .out7(demultiplexer_2_out7), .in(Load), .sel(Addr3));
  Register #(.trigger("falling"), .width(16)) register_1 (
    .D(demultiplexer_1_out0), .en(demultiplexer_2_out0), .clk(demultiplexer_3_out0), .Q(register_1_q));  // open: clr
  Register #(.trigger("falling"), .width(16)) register_2 (
    .D(demultiplexer_1_out1), .en(demultiplexer_2_out1), .clk(demultiplexer_3_out1), .Q(register_2_q));  // open: clr
  Register #(.trigger("falling"), .width(16)) register_3 (
    .D(demultiplexer_1_out2), .en(demultiplexer_2_out2), .clk(demultiplexer_3_out2), .Q(register_3_q));  // open: clr
  Register #(.trigger("falling"), .width(16)) register_4 (
    .D(demultiplexer_1_out3), .en(demultiplexer_2_out3), .clk(demultiplexer_3_out3), .Q(register_4_q));  // open: clr
  Demultiplexer #(.select(3)) demultiplexer_3 (
    .out0(demultiplexer_3_out0), .out1(demultiplexer_3_out1), .out2(demultiplexer_3_out2),
    .out3(demultiplexer_3_out3), .out4(demultiplexer_3_out4), .out5(demultiplexer_3_out5),
    .out6(demultiplexer_3_out6), .out7(demultiplexer_3_out7), .in(Clock), .sel(Addr3));
  Register #(.trigger("falling"), .width(16)) register_5 (
    .D(demultiplexer_1_out4), .en(demultiplexer_2_out4), .clk(demultiplexer_3_out4), .Q(register_5_q));  // open: clr
  Register #(.trigger("falling"), .width(16)) register_6 (
    .D(demultiplexer_1_out5), .en(demultiplexer_2_out5), .clk(demultiplexer_3_out5), .Q(register_6_q));  // open: clr
  Register #(.trigger("falling"), .width(16)) register_7 (
    .D(demultiplexer_1_out6), .en(demultiplexer_2_out6), .clk(demultiplexer_3_out6), .Q(register_7_q));  // open: clr
  Register #(.trigger("falling"), .width(16)) register_8 (
    .D(demultiplexer_1_out7), .en(demultiplexer_2_out7), .clk(demultiplexer_3_out7), .Q(register_8_q));  // open: clr
  Multiplexer #(.select(3), .width(16)) multiplexer_1 (
    .in0(register_1_q), .in1(register_2_q), .in2(register_3_q), .in3(register_4_q), .in4(register_5_q),
    .in5(register_6_q), .in6(register_7_q), .in7(register_8_q), .out(multiplexer_1_out), .sel(Addr3));
  // Probe on multiplexer_1_out
endmodule

module ProgramCounter (
  input  [15:0] Input16,
  input  Load,
  input  Inc,
  input  Clock,
  input  Reset,
  output [15:0] Output16
);

  wire multiplexer_2_out, not_1_out;
  wire [15:0] adder_1_out, multiplexer_1_out;

  not not_1 (not_1_out, 1'b1);
  Multiplexer #(.select(2), .width(16)) multiplexer_1 (
    .in0(Input16), .in1(adder_1_out), .in2(Input16), .in3(Input16), .out(multiplexer_1_out), .sel({Load, Inc}));
  // Probe on multiplexer_1_out
  Multiplexer #(.select(2)) multiplexer_2 (
    .in0(not_1_out), .in1(Inc), .in2(Load), .in3(not_1_out), .out(multiplexer_2_out), .sel({Load, Inc}));
  Register #(.trigger("falling"), .width(16)) register_1 (
    .D(multiplexer_1_out), .en(multiplexer_2_out), .clk(Clock), .Q(Output16), .clr(Reset));
  // Probe on Output16
  // Probe on adder_1_out
  Adder #(.width(16)) adder_1 (.a(Output16), .b(16'h1), .out(adder_1_out));  // open: cin, cout
endmodule
